# Fritzing sketch BreadBoardConnections (saved by Fritzing 0.9.3b)
breadboards: 1

parts:
  R1 = Rotary Potentiometer (Large) [maximum_resistance=100kΩ package=THT]
  Part1 = Arduino Uno (Rev3) - ICSP
  S1 = Momentary Switch [package=ksa_sealed_tac_switch]
  S2 = Pushbutton [package="[SMD]"]
  J1 = Piezo Speaker
  Part2 = Real Time Clock Module - DS1307 RTC Breakout Board
  R2 = Resistor [tolerance=±5% resistance=10k package=THT]
  R3 = Resistor [tolerance=±5% resistance=10k package=THT]

nets:
  5V: R1.leg1, Part1.5V, S1.3, S2.Pin_3, S2.Pin_4, Part2.5V
  N1: R1.wiper, Part1.A0
  GND: R1.leg2, Part1.GND, J1.pin1, Part2.GND, R2.Pin_0, R3.Pin_0
  N2: Part1.A4/SDA, Part2.SDA
  N3: Part1.A5/SCL, Part2.SCL
  N4: Part1.D2, J1.pin2
  N5: Part1.D4, S2.Pin_1, S2.Pin_2, R3.Pin_1
  N6: Part1.D7, S1.1, R2.Pin_1
